# Fritzing sketch designer (saved by Fritzing 0.9.3b)
breadboards: 1

parts:
  Composant1 = Arduino Uno (Rev3)
  J1 = Basic Servo
  J2 = Basic Servo
  VCC1 = Battery block 9V
  R1 = Rotary Potentiometer (Small) [maximum_resistance=100kΩ package=THT]

nets:
  N1: Composant1.A0, R1.wiper
  N2: Composant1.D9_PWM, J1.pulse
  GND: Composant1.GND, J1.gnd, J2.gnd, VCC1.-, R1.leg2
  N3: Composant1.D6_PWM, J2.pulse
  VCC: J1.vcc, J2.vcc, VCC1.+, R1.leg1
